// Logisim project data_path.circ as structural Verilog: 1 circuit, main circuit main
module main (
  input  stall_or_kill,
  input  in_2,
  output [31:0] out_3,
  output [31:0] out_4,
  output [31:0] out_5,
  output [31:0] out_6,
  output [31:0] out_7,
  output [31:0] out_8,
  output [31:0] out_9,
  output [31:0] out_10,
  output [31:0] out_11,
  output [31:0] out_12,
  output [31:0] out_13,
  output [31:0] out_14,
  output [31:0] out_15,
  output [31:0] out_16,
  output [31:0] out_17,
  output [31:0] out_18,
  output [31:0] out_19,
  output [31:0] out_20,
  output [31:0] out_21,
  output [31:0] out_22,
  output [31:0] out_23,
  output [31:0] out_24,
  output [31:0] out_25,
  output [31:0] out_26,
  output [31:0] out_27,
  output [31:0] out_28,
  output [31:0] out_29,
  output [31:0] out_30,
  output [31:0] out_31,
  output [31:0] out_32,
  output [31:0] out_33,
  output [31:0] out_34,
  output [31:0] out_35,
  output out_36,
  output out_37
);

  wire clock, Extop, Extop_Ex, jalr, jalr_EX, jalr_MEM, kill, LessFlagSigned, LessFlagUnsigned,
       main_9_mem_to_reg, main_9_memory_read, main_9_memory_write, main_9_regwrite, mem_to_reg,
       mem_to_reg_EX, mem_to_reg_MEM, mem_to_reg_WB, Memory_Write, Memory_Write_EX, Memory_Write_MEM,
       MemRead, MemRead_EX, MemRead_MEM, or_1_out, pc_src, RegWrite, RegWrite_EX, RegWrite_Ex_t,
       RegWrite_MEM, RegWrite_WB, SSET, Stall, ZeroFlag;
  wire [1:0] ALUsrc, ALUsrc_EX;
  wire [4:0] ImmL, ImmL_Ex, ImmL_ID, multiplexer_4_out, Rd_WB, Rd_WB_EX, Rd_WB_MEM, Rs1_Ex, Rs1_ID, Rs2_Ex,
       Rs2_ID;
  wire [5:0] OP;
  wire [7:0] ALU_Op, ALU_Op_Ex;
  wire [10:0] Funct, ImmU, ImmU_Ex;
  wire [15:0] Imm16, Imm16_Ex, Imm16_ID;
  wire [19:0] pc, PC_ID, pc_inc, pc_inc_EX, pc_inc_Ex_t, pc_inc_ID, pc_inc_MEM;
  wire [31:0] ALU_Result, ALU_Result_EX, ALU_Result_MEM, ALU_Result_WB, bit_extender_1_out,
       bit_extender_2_out, bit_extender_3_out, bit_extender_4_out, BusA, BusA_Ex, BusB, BusB_EX, BusB_Ex_t,
       BusB_MEM, main_2_out_2, main_3_instruction_2, MEM_Data_EX, MEM_Data_MEM, MEM_Data_WB,
       multiplexer_1_out, multiplexer_2_out, multiplexer_3_out, multiplexer_5_out, Write_Data;

  // Probe on pc_inc
  pc_circut_main main_1 (
    .pc_src(pc_src), .out_10(pc_inc), .Lower5(ImmL_ID), .upper11(Funct), .IMM16(Imm16), .in_4(clock),
    .RS1(BusA), .jalr(jalr), .out_11(pc), .stall(Stall), .PC_ID(PC_ID));
  // Probe on pc
  // Probe on pc
  Clock clock_1 (.out(clock));
  instruction_mem_main main_2 (.in_1(pc), .out_2(main_2_out_2));
  Multiplexer #(.width(32), .enable("false")) multiplexer_1 (
    .in0(main_2_out_2), .in1({32{1'b0}}), .out(multiplexer_1_out), .sel(kill));
  // Probe on Imm16
  // Probe on ImmL
  // Probe on ImmU
  IF_ID_REGISTER_main main_3 (
    .instruction(multiplexer_1_out), .PC_IF(pc), .pc_inc(pc_inc), .clk(clock), .stall(Stall),
    .instruction_2(main_3_instruction_2), .PC_ID(PC_ID), .pc_inc_2(pc_inc_ID));
  assign bit_extender_1_out = {{16{1'b0}}, Imm16};  // Bit_Extender bit_extender_1
  assign bit_extender_2_out = {{16{Imm16[15]}}, Imm16};  // Bit_Extender bit_extender_2
  assign bit_extender_3_out = {{16{ImmU[10]}}, {ImmU, ImmL}};  // Bit_Extender bit_extender_3
  Multiplexer #(.width(32), .enable("false")) multiplexer_2 (
    .in0(bit_extender_1_out), .in1(bit_extender_2_out), .out(multiplexer_2_out), .sel(Extop));
  // Fetch_instruction_main main_4: pin names not known; wires that end beside it: Imm16_ID, Rs1_ID, Rs2_ID, main_3_instruction_2, ImmL_ID, OP, Funct
  Multiplexer #(.select(2), .width(32), .enable("false")) multiplexer_3 (
    .in0(BusB), .in1(multiplexer_2_out), .in2(bit_extender_3_out), .out(multiplexer_3_out), .sel(ALUsrc));  // open: in3
  // Probe on ALU_Op[5:4]
  // Probe on Rs1_ID
  ALU_Full alu_full_1 (
    .OverFlow(out_36), .AInvert(ALU_Op[7]), .CarryIn(ALU_Op[6]), .in_2(BusA), .in_4(multiplexer_3_out),
    .Operation(ALU_Op[5:4]), .BInvert(ALU_Op[6]), .select_Alu(ALU_Op[3:0]),
    .less_flag_signed(LessFlagUnsigned), .out_11(LessFlagSigned), .out_9(ALU_Result), .out_14(out_37),
    .zreo_flag(ZeroFlag));  // open: in_5
  Multiplexer #(.width(5), .enable("false")) multiplexer_4 (
    .in0(Rs1_ID), .in1(Rd_WB), .out(multiplexer_4_out), .sel(SSET));
  // Probe on ALU_Result
  // EX_MEM_Register_main main_5: pin names not known; wires that end beside it: ALU_Result_EX, BusB_EX, MemRead_EX, Memory_Write_EX, mem_to_reg_EX, Rd_WB_EX, RegWrite_EX, pc_inc_EX, jalr_EX, clock
  // Probe on Write_Data
  // Probe on OP
  // Probe on ALU_Result_MEM
  // Reg_file reg_file_1: pin names not known; wires that end beside it: multiplexer_4_out, Rs2_ID, Rd_WB, clock, out_3, out_4, out_6, out_8, out_11, RegWrite, out_13, out_15, out_17, out_19, out_21, out_23, out_25, Write_Data, out_27, out_29, out_31, out_33, out_35, out_5, out_7, out_9, out_12, out_14, out_16, out_18, out_20, out_22, out_24, out_26, out_28, out_30, out_32, out_34, BusA, BusB
  // Probe on BusB
  data_mem_main main_6 (
    .in_1(ALU_Result_MEM), .in_2(Memory_Write_MEM), .in_3(MemRead_MEM), .in_4(clock),
    .memory_output(MEM_Data_EX), .in_5(BusB_MEM));
  ID_EX_Reg_main main_7 (
    .PC_Inc(pc_inc_ID), .RS1(Rs1_ID), .RS2(Rs2_ID), .RD(Rd_WB), .BusA(BusA), .BusB(BusB), .in_7(clock),
    .RegWrite(RegWrite), .Imm16(Imm16), .ImmL(ImmL), .ImmU(ImmU), .ExtOp(Extop), .ALUSrc(ALUsrc),
    .ALUOp(ALU_Op), .MemRead(MemRead), .MemWrite(Memory_Write), .MemToReg(mem_to_reg), .out_19(pc_inc_Ex_t),
    .out_20(Rs1_Ex), .out_21(Rs2_Ex), .out_22(Rd_WB), .out_23(BusA_Ex), .out_24(BusB_Ex_t),
    .out_25(RegWrite_Ex_t), .out_26(Imm16_Ex), .out_27(ImmL_Ex), .out_28(ImmU_Ex), .out_29(Extop_Ex),
    .out_30(ALUsrc_EX), .out_31(ALU_Op_Ex), .out_32(MemRead_EX), .out_33(Memory_Write_EX),
    .out_34(mem_to_reg_EX), .jalr(jalr), .out_35(jalr_EX));
  // MEM_WB_Register_main main_8: pin names not known; wires that end beside it: ALU_Result_MEM, MEM_Data_MEM, mem_to_reg_MEM, RegWrite_MEM, Rd_WB_MEM, pc_inc_MEM, jalr_MEM, clock, ALU_Result_WB, MEM_Data_WB, mem_to_reg_WB, RegWrite_WB, Rd_WB, pc_inc_MEM, jalr_MEM
  MainControlUnit_main main_9 (
    .ALU_Op(ALU_Op), .mem_to_reg(main_9_mem_to_reg), .Memory_Read(main_9_memory_read),
    .Memory_Write(main_9_memory_write), .RegWrite(main_9_regwrite), .in_1(Funct), .Extop(Extop),
    .ALUsrc(ALUsrc), .in_2(OP), .SSET(SSET), .jalr(jalr), .Pc_src(pc_src), .ZeroFlag(ZeroFlag),
    .LessFlagSigned(LessFlagSigned), .LessFlagUnsigned(LessFlagUnsigned));
  // Probe on ALU_Result_WB
  Multiplexer #(.width(32), .enable("false")) multiplexer_5 (
    .in0(ALU_Result_WB), .out(multiplexer_5_out), .sel(mem_to_reg_WB));  // open: in1
  Multiplexer #(.enable("false")) multiplexer_6 (.in0(main_9_mem_to_reg), .in1(1'b0), .out(mem_to_reg), .sel(or_1_out));
  Multiplexer #(.enable("false")) multiplexer_7 (.in0(main_9_memory_read), .in1(1'b0), .out(MemRead), .sel(or_1_out));
  Multiplexer #(.enable("false")) multiplexer_8 (
    .in0(main_9_memory_write), .in1(1'b0), .out(Memory_Write), .sel(or_1_out));
  Multiplexer #(.enable("false")) multiplexer_9 (.in0(main_9_regwrite), .in1(1'b0), .out(RegWrite), .sel(or_1_out));
  assign bit_extender_4_out = {{12{1'b0}}, pc_inc_MEM};  // Bit_Extender bit_extender_4
  or or_1 (or_1_out, stall_or_kill, in_2);
  Multiplexer #(.width(32), .enable("false")) multiplexer_10 (
    .in0(multiplexer_5_out), .in1(bit_extender_4_out), .out(Write_Data), .sel(jalr_MEM));

  assign out_10 = out_9;

  // Other names for the same wires on the sheet: ImmU_ID[10:0] = Funct; R0[31:0] = out_3; R1[31:0] = out_4;
  //   R2[31:0] = out_6; R3[31:0] = out_8; R4[31:0] = out_11; R5[31:0] = out_13; R6[31:0] = out_15; R7[31:0] = out_17;
  //   R8[31:0] = out_19; R9[31:0] = out_21; R10[31:0] = out_23; R11[31:0] = out_25; R12[31:0] = out_27;
  //   R13[31:0] = out_29; R14[31:0] = out_31; R15[31:0] = out_33; R16[31:0] = out_35; R17[31:0] = out_5;
  //   R18[31:0] = out_7; R19[31:0] = out_9; R20[31:0] = out_12; R21[31:0] = out_14; R22[31:0] = out_16;
  //   R23[31:0] = out_18; R24[31:0] = out_20; R25[31:0] = out_22; R26[31:0] = out_24; R27[31:0] = out_26;
  //   R28[31:0] = out_28; R29[31:0] = out_30; R30[31:0] = out_32; R31[31:0] = out_34; Rd_ID[4:0] = ImmL_ID

  // Notes on the sheet:
  //   Registers
  //   IF
  //   EX
  //   signal
  //   ID
  //   MEM
  //   WB
endmodule
